# Fritzing sketch Sketch1 (saved by Fritzing 0.9.4)
breadboards: 1

parts:
  Part1 = Arduino Mega 2560 (Rev3)
  Pololu_A1 = Pololu A4988 [package=SO16]
  LCD2004-I2C1 = LCD2004-I2C
  kEYPAD_MATRICIAL_1 = KEYPAD 4x3
  ZS-042_RTC1 = ZS-042 RTC Module
  microSD1 = MicroSD Card Module  # not connected
  U1 = LIPO-2000mAh [package=lipo-2000]
  M1 = Stepper Motor - Bipolar
  C1 = Electrolytic Capacitor [capacitance=0.1mF voltage=16V package="100 mil [THT, electrolytic]"]

nets:
  N1: Part1.D21/SCL, Part1.SCL, LCD2004-I2C1.SCL, ZS-042_RTC1.SCL
  N2: Part1.D20/SDA, Part1.SDA, LCD2004-I2C1.SDA, ZS-042_RTC1.SDA
  VCC: Part1.5V, Pololu_A1.VDD, LCD2004-I2C1.VCC, ZS-042_RTC1.VCC
  GND: Part1.GND, Pololu_A1.GND#8, LCD2004-I2C1.GND, ZS-042_RTC1.GND
  N3: Part1.D33, kEYPAD_MATRICIAL_1.arrow4
  N4: Part1.D35, kEYPAD_MATRICIAL_1.arrow3
  N5: Part1.D37, kEYPAD_MATRICIAL_1.col3
  N6: Part1.D39, kEYPAD_MATRICIAL_1.arrow2
  N7: Part1.D41, kEYPAD_MATRICIAL_1.col2
  N8: Part1.D43, kEYPAD_MATRICIAL_1.arrow1
  N9: Part1.D45, kEYPAD_MATRICIAL_1.col1
  N10: Pololu_A1.1B, M1.A
  N11: Pololu_A1.1A, M1.C
  N12: Pololu_A1.2A, M1.B
  N13: Pololu_A1.2B, M1.D
  N14: Pololu_A1.GND#14, U1.-, C1.-
  N15: Pololu_A1.VMOT, U1.+, C1.+

custom parts:
  LCD2004-I2C: A standard character display with 4x20 characters. Comes in many colors with LCM2004 IIC attached.
  KEYPAD 4x3: KEYPAD matricial de 12 botones, 4 filas x 3 columnas
